# Fritzing sketch Complete (saved by Fritzing 0.9.3b)
breadboards: 2

parts:
  Bauteil1 = Arduino Mega 2560 (Rev3)
  IC1 = ULN2803A [package=THT]  # not connected
  IC2 = ULN2803A [package=THT]  # not connected
  IC3 = ULN2803A [package=THT]  # not connected
  IC4 = ULN2803A [package=THT]  # not connected
  J1 = Power Jack [package=power_jack_smd]
  DCF77_Receiver = IC, SIP package, 4 pins [chip_label=DCF77]

nets:
  GND: Bauteil1.GND, J1.GND, J1.GNDBREAK, DCF77_Receiver.pin1, DCF77_Receiver.pin3
  N1: Bauteil1.3V3, DCF77_Receiver.pin4
  N2: Bauteil1.VIN, J1.PWR
  N3: Bauteil1.D0_RX0, DCF77_Receiver.pin2

notes:
  <- 3.3 V
  <- 9 V
